// Logisim project mips-like.circ as structural Verilog: 4 circuits, main circuit PROCESSADOR
module PROCESSADOR (
  output [31:0] \INSTRUÇÃO 
);

  wire Bit_Brunch, Branch, Branch_UC, button_1_out, clock_1_out, Jump, LI, Mem_Load, Mem_Read, U_I,
       UC_write_reg;
  wire [3:0] ULA_OP;
  wire [7:0] bit_extender_2_out, PC_q_2;
  wire [31:0] adder_1_out, adder_2_out, banco_de_registradores_1_r0_d, banco_de_registradores_1_r1_d,
       Bit_Imediato, multiplexer_1_out, multiplexer_2_out, multiplexer_3_out, multiplexer_4_out, PC_q,
       ram_1_data, shifter_1_out, shifter_2_out, ula_1_ula_out;

  Adder #(.width(32)) adder_1 (.a({PC_q[31:10], PC_q_2, PC_q[1:0]}), .b(32'h4), .out(adder_1_out));  // open: cin, cout
  Shifter #(.width(32)) shifter_1 (.in(Bit_Imediato), .\dist (5'b00010), .out(shifter_1_out));
  Shifter #(.width(32)) shifter_2 (.in(Bit_Imediato), .\dist (5'b00010), .out(shifter_2_out));
  Adder #(.width(32)) adder_2 (.a(adder_1_out), .b(shifter_1_out), .out(adder_2_out));  // open: cin, cout
  Multiplexer #(.width(32), .enable("false")) multiplexer_1 (
    .in0(adder_1_out), .in1(adder_2_out), .out(multiplexer_1_out), .sel(Branch));
  Multiplexer #(.width(32), .enable("false")) multiplexer_2 (
    .in0(multiplexer_1_out), .in1(shifter_2_out), .out(multiplexer_2_out), .sel(Jump));
  Clock clock_1 (.out(clock_1_out));
  Register #(.width(32)) PC (
    .D(multiplexer_2_out), .Q({PC_q[31:10], PC_q_2, PC_q[1:0]}), .clk(clock_1_out), .clr(button_1_out));  // open: en
  Button button_1 (.out(button_1_out));
  ROM #(.dataWidth(32)) rom_1 (.addr(PC_q_2), .data(\INSTRUÇÃO ));  // open: sel
  Multiplexer #(.width(32), .enable("false")) multiplexer_3 (
    .in0(multiplexer_4_out), .in1(Bit_Imediato), .out(multiplexer_3_out), .sel(LI));
  UC UC (
    .E3(\INSTRUÇÃO [31]), .E2(\INSTRUÇÃO [30]), .E1(\INSTRUÇÃO [29]), .E0(\INSTRUÇÃO [28]), .out_5(ULA_OP),
    .write_reg(UC_write_reg), .Usa_imediate(U_I), .Jump(Jump), .Branch(Branch_UC), .Mem_Read(Mem_Read),
    .Mem_Reg(Mem_Load), .LI(LI));
  BANCO_DE_REGISTRADORES banco_de_registradores_1 (
    .DATA_WRITE(multiplexer_3_out), .CLK(clock_1_out), .RW(\INSTRUÇÃO [27:24]),
    .R0_D(banco_de_registradores_1_r0_d), .R0(\INSTRUÇÃO [19:16]), .R1_D(banco_de_registradores_1_r1_d),
    .R1(\INSTRUÇÃO [23:20]), .RW_bit(UC_write_reg), .RESET(button_1_out));
  assign Bit_Imediato = {{16{1'b0}}, \INSTRUÇÃO [15:0]};  // Bit_Extender bit_extender_1
  Multiplexer #(.width(32), .enable("false")) multiplexer_4 (
    .in0(ula_1_ula_out), .in1(ram_1_data), .out(multiplexer_4_out), .sel(Mem_Read));
  ULA ula_1 (
    .DATA_0(banco_de_registradores_1_r0_d), .DATA_1(banco_de_registradores_1_r1_d), .ULA_OUT(ula_1_ula_out),
    .ULA_OP(ULA_OP), .Imediato(Bit_Imediato), .U_I(U_I), .Bit_Brunch(Bit_Brunch));
  and and_1 (Branch, Bit_Brunch, Branch_UC);
  Bit_Extender #(.in_width(32), .out_width(8)) bit_extender_2 (.in(ula_1_ula_out), .out(bit_extender_2_out));
  RAM #(.dataWidth(32), .bus("separate")) ram_1 (
    .addr(bit_extender_2_out), .din(banco_de_registradores_1_r1_d), .data(ram_1_data), .str(Mem_Load),
    .clk(clock_1_out), .ld(Mem_Read));  // open: sel, clr

  // Notes on the sheet:
  //   contents of rom_1 (hex, n*v repeats v):
  //   61000000 62000001 63000004 30130017 64000000 30430013 65000000 3053000f 52020001 4d010002 4e050002
  //   6d40000 7d50000 8e40000 6c000000 79c70000 7ac80010 7bc60020 299a0000 99b0000 80960020 55050001
  //   90000007 54040001 90000005 51010001 90000003
  //   REG_0
  //   REG_1
  //   REG_W
  //   DATA_W
  //   BANCO DE REGISTRADORES
  //   REG0_D
  //   REG1_D
  //   ULA
endmodule

module ULA (
  input  [31:0] DATA_0,
  input  U_I,
  input  [3:0] ULA_OP,
  input  [31:0] DATA_1,
  input  [31:0] Imediato,
  output [31:0] ULA_OUT,
  output Bit_Brunch
);

  wire [2:0] Op;
  wire [4:0] bit_extender_1_out;
  wire [31:0] A_comp, A_mul, A_soma, A_sub, B_comp, B_mul, B_soma, B_sub, demultiplexer_1_out5, Equals,
       multiplexer_1_out, Prod, SLL_A, SLL_OUT, Soma, Subt;

  Demultiplexer #(.select(3), .width(32), .enable("false")) demultiplexer_1 (
    .out0(A_soma), .out1(A_sub), .out2(A_mul), .out3(A_comp), .out4(SLL_A), .out5(demultiplexer_1_out5),
    .in(DATA_0), .sel(Op));  // open: out6, out7
  Demultiplexer #(.select(3), .width(32), .enable("false")) demultiplexer_2 (
    .out0(B_soma), .out1(B_sub), .out2(B_mul), .out3(B_comp), .in(DATA_1), .sel(Op));  // open: out4, out5, out6, out7
  Multiplexer #(.width(32), .enable("false")) multiplexer_1 (
    .in0(B_soma), .in1(Imediato), .out(multiplexer_1_out), .sel(U_I));
  Bit_Extender #(.in_width(32), .out_width(5)) bit_extender_1 (.in(Imediato), .out(bit_extender_1_out));
  Adder #(.width(32)) adder_1 (.a(A_soma), .b(multiplexer_1_out), .out(Soma));  // open: cin, cout
  Subtractor #(.width(32)) subtractor_1 (.a(A_sub), .b(B_sub), .out(Subt));  // open: bin, bout
  Multiplier #(.width(32)) multiplier_1 (.a(A_mul), .b(B_mul), .out(Prod));  // open: cin, cout
  Comparator #(.width(32), .mode("unsigned")) comparator_1 (.a(A_comp), .b(B_comp), .eq(Bit_Brunch));  // open: gt, lt
  Shifter #(.width(32)) shifter_1 (.in(SLL_A), .\dist (bit_extender_1_out), .out(SLL_OUT));
  assign Equals = {{31{1'b0}}, Bit_Brunch};  // Bit_Extender bit_extender_2
  Multiplexer #(.select(3), .width(32), .enable("false")) multiplexer_2 (
    .in0(Soma), .in1(Subt), .in2(Prod), .in3(Equals), .in4(SLL_OUT), .in5(A_soma), .in6(A_soma),
    .in7(A_soma), .out(ULA_OUT), .sel(Op));
  Bit_Extender #(.in_width(4), .out_width(3)) bit_extender_3 (.in(ULA_OP), .out(Op));

  // Other names for the same wires on the sheet: Imediate[31:0] = Imediato
endmodule

module UC (
  input  E3,
  input  E2,
  input  E1,
  input  E0,
  output [3:0] out_5,
  output write_reg,
  output Usa_imediate,
  output Jump,
  output Branch,
  output Mem_Read,
  output Mem_Reg,
  output LI
);

  wire and_1_out, and_2_out, and_3_out, and_4_out, and_5_out, and_6_out, and_7_out, and_8_out, and_9_out,
       and_10_out, and_11_out, and_12_out, and_14_out, and_15_out, and_17_out, and_18_out, and_19_out,
       and_20_out, and_21_out, not_1_out, not_2_out, not_3_out, not_4_out, not_5_out, not_6_out, not_7_out,
       not_8_out, not_9_out, not_10_out, not_11_out, not_12_out, not_13_out, not_14_out, not_15_out,
       not_16_out, not_17_out, not_18_out;

  and and_1 (and_1_out, E3, E0);
  and and_2 (and_2_out, E3, E1);
  and and_3 (and_3_out, E3, E2);
  and and_4 (and_4_out, E2, not_1_out);
  not not_1 (not_1_out, E0);
  and and_5 (and_5_out, E3, E1);
  not not_2 (not_2_out, E2);
  and and_6 (and_6_out, not_2_out, E1);
  and and_7 (and_7_out, E1, not_3_out);
  not not_3 (not_3_out, E0);
  and and_8 (and_8_out, E3, E1);
  not not_4 (not_4_out, E2);
  and and_9 (and_9_out, not_4_out, E0);
  and and_10 (and_10_out, E3, E1);
  not not_5 (not_5_out, E3);
  and and_11 (and_11_out, not_5_out, not_6_out);
  not not_6 (not_6_out, E1);
  and and_12 (and_12_out, E1, not_7_out);
  not not_7 (not_7_out, E0);
  not not_8 (not_8_out, E3);
  not not_9 (not_9_out, E1);
  not not_10 (not_10_out, E2);
  not not_11 (not_11_out, E1);
  not not_12 (not_12_out, E0);
  not not_13 (not_13_out, E2);
  not not_14 (not_14_out, E1);
  not not_15 (not_15_out, E2);
  and and_13 (Branch, not_15_out, E1, E0);
  and and_14 (and_14_out, E2, E1, E0);
  and and_15 (and_15_out, E3, E1);
  and and_16 (Mem_Reg, E3, not_16_out);
  not not_16 (not_16_out, E0);
  not not_17 (not_17_out, E3);
  not not_18 (not_18_out, E0);
  or or_1 (out_5[3], and_1_out, and_2_out, and_3_out);
  or or_2 (out_5[2], and_4_out, and_5_out);
  or or_3 (out_5[1], and_6_out, and_7_out, and_8_out);
  or or_4 (out_5[0], and_9_out, and_10_out);
  or or_5 (write_reg, and_11_out, and_12_out, E2);
  and and_17 (and_17_out, not_8_out, E2, not_9_out);
  and and_18 (and_18_out, E2, E1, E0);
  or or_6 (Usa_imediate, and_17_out, and_18_out, and_19_out);
  and and_19 (and_19_out, E3, not_10_out, not_11_out, not_12_out);
  and and_20 (and_20_out, E3, not_13_out, not_14_out, E0);
  or or_7 (Jump, and_20_out, and_21_out);
  and and_21 (and_21_out, E3, E2, E1);
  or or_8 (Mem_Read, and_14_out, and_15_out);
  and and_22 (LI, not_17_out, E2, E1, not_18_out);
endmodule

module BANCO_DE_REGISTRADORES (
  input  [31:0] DATA_WRITE,
  input  [3:0] R0,
  input  CLK,
  input  [3:0] RW,
  input  RW_bit,
  input  [3:0] R1,
  input  RESET,
  output [31:0] R0_D,
  output [31:0] R1_D
);

  wire E0, E1, E2, E3, E4, E5, E6, E7, E8, E9, E10, E11, E12, E13, E14, E15;
  wire [31:0] S0, S1, S2, S3, S4, S5, S6, S7, S8, S9, S10, S11, S12, S13, S14, S15;

  Demultiplexer #(.select(4), .enable("false")) demultiplexer_1 (
    .out0(E0), .out1(E1), .out2(E2), .out3(E3), .out4(E4), .out5(E5), .out6(E6), .out7(E7), .out8(E8),
    .out9(E9), .out10(E10), .out11(E11), .out12(E12), .out13(E13), .out14(E14), .out15(E15), .in(RW_bit),
    .sel(RW));
  Register #(.width(32)) register_1 (.D(DATA_WRITE), .en(E0), .Q(S0), .clk(CLK), .clr(RESET));
  Register #(.width(32)) register_2 (.D(DATA_WRITE), .en(E4), .Q(S4), .clk(CLK), .clr(RESET));
  Register #(.width(32)) register_3 (.D(DATA_WRITE), .en(E8), .Q(S8), .clk(CLK), .clr(RESET));
  Register #(.width(32)) register_4 (.D(DATA_WRITE), .en(E12), .Q(S12), .clk(CLK), .clr(RESET));
  Register #(.width(32)) register_5 (.D(DATA_WRITE), .en(E1), .Q(S1), .clk(CLK), .clr(RESET));
  Register #(.width(32)) register_6 (.D(DATA_WRITE), .en(E5), .Q(S5), .clk(CLK), .clr(RESET));
  Register #(.width(32)) register_7 (.D(DATA_WRITE), .en(E9), .Q(S9), .clk(CLK), .clr(RESET));
  Register #(.width(32)) register_8 (.D(DATA_WRITE), .en(E13), .Q(S13), .clk(CLK), .clr(RESET));
  Register #(.width(32)) register_9 (.D(DATA_WRITE), .en(E2), .Q(S2), .clk(CLK), .clr(RESET));
  Register #(.width(32)) register_10 (.D(DATA_WRITE), .en(E6), .Q(S6), .clk(CLK), .clr(RESET));
  Register #(.width(32)) register_11 (.D(DATA_WRITE), .en(E10), .Q(S10), .clk(CLK), .clr(RESET));
  Register #(.width(32)) register_12 (.D(DATA_WRITE), .en(E14), .Q(S14), .clk(CLK), .clr(RESET));
  Register #(.width(32)) register_13 (.D(DATA_WRITE), .en(E3), .Q(S3), .clk(CLK), .clr(RESET));
  Register #(.width(32)) register_14 (.D(DATA_WRITE), .en(E7), .Q(S7), .clk(CLK), .clr(RESET));
  Register #(.width(32)) register_15 (.D(DATA_WRITE), .en(E11), .Q(S11), .clk(CLK), .clr(RESET));
  Register #(.width(32)) register_16 (.D(DATA_WRITE), .en(E15), .Q(S15), .clk(CLK), .clr(RESET));
  Multiplexer #(.select(4), .width(32), .disabled(0), .enable("false")) multiplexer_1 (
    .in0(S0), .in1(S1), .in2(S2), .in3(S3), .in4(S4), .in5(S5), .in6(S6), .in7(S7), .in8(S8), .in9(S9),
    .in10(S10), .in11(S11), .in12(S12), .in13(S13), .in14(S14), .in15(S15), .out(R0_D), .sel(R0));
  Multiplexer #(.select(4), .width(32), .enable("false")) multiplexer_2 (
    .in0(S0), .in1(S1), .in2(S2), .in3(S3), .in4(S4), .in5(S5), .in6(S6), .in7(S7), .in8(S8), .in9(S9),
    .in10(S10), .in11(S11), .in12(S12), .in13(S13), .in14(S14), .in15(S15), .out(R1_D), .sel(R1));

  // Other names for the same wires on the sheet: A_WRITE[31:0] = DATA_WRITE
endmodule
